// Logisim project lab_5.circ as structural Verilog: 19 circuits, main circuit shifrator
module shifrator (
  input  in_1,
  input  in_2,
  input  in_3,
  input  in_4,
  input  _0,
  input  _1,
  input  _2,
  input  _3,
  input  _4,
  input  _5,
  input  _6,
  input  _7,
  input  _8,
  input  _9,
  input  _10,
  input  _11,
  input  _12,
  input  _13,
  input  _14,
  input  _15,
  output out_21,
  output out_22,
  output out_23,
  output out_24,
  output out_25
);

  wire not_1_out, or_1_out, or_2_out, or_3_out, or_4_out, or_5_out, xnor_1_out;

  or or_1 (or_1_out, _7, _14, _12, _10, _8, _6, _4, _2, _15, _13, _11, _9, _5, _3, _1, _0);
  NotExactlyOne xnor_1 (
    .out(xnor_1_out), .in0(_7), .in1(_14), .in2(_12), .in3(_10), .in4(_8), .in5(_6), .in6(_4), .in7(_2),
    .in8(_15), .in9(_13), .in10(_11), .in11(_9), .in12(_5), .in13(_3), .in14(_1), .in15(_0));
  and and_1 (out_21, or_1_out, xnor_1_out);
  not not_1 (not_1_out, out_21);
  or or_2 (or_2_out, _1, _3, _5, _7, _9, _11, _13, _15);
  or or_3 (or_3_out, _2, _3, _6, _7, _10, _11, _14, _15);
  or or_4 (or_4_out, _4, _5, _6, _7, _12, _13, _14, _15);
  or or_5 (or_5_out, _8, _9, _10, _11, _12, _13, _14, _15);
  and and_2 (out_25, or_2_out, not_1_out);
  and and_3 (out_24, or_3_out, not_1_out);
  and and_4 (out_23, or_4_out, not_1_out);
  and and_5 (out_22, or_5_out, not_1_out);
  ExactlyOne xor_1 (.in0(in_1), .in2(in_2), .in3(in_4), .in4(in_3));  // open: out
endmodule

module deshifrator (
  input  in_1,
  input  in_2,
  input  in_3,
  input  in_4
);

  wire and_1_out, and_2_out, and_3_out, and_4_out, and_5_out, and_6_out, and_7_out, and_8_out, and_9_out,
       and_10_out, and_11_out, and_12_out, and_13_out, and_14_out, and_15_out, and_16_out, not_1_out,
       not_2_out, not_3_out, not_4_out, or_1_out, or_2_out, or_3_out, or_4_out, or_5_out, or_6_out, or_7_out;

  not not_1 (not_1_out, in_4);
  not not_2 (not_2_out, in_3);
  not not_3 (not_3_out, in_2);
  not not_4 (not_4_out, in_1);
  and and_1 (and_1_out, not_4_out, not_3_out, not_2_out, not_1_out);
  and and_2 (and_2_out, not_4_out, not_3_out, not_2_out, in_4);
  and and_3 (and_3_out, not_4_out, not_3_out, in_3, in_4);
  and and_4 (and_4_out, not_4_out, not_3_out, in_3, not_1_out);
  and and_5 (and_5_out, not_4_out, in_2, not_2_out, not_1_out);
  and and_6 (and_6_out, not_4_out, in_2, not_2_out, in_4);
  and and_7 (and_7_out, not_4_out, in_2, in_3, not_1_out);
  and and_8 (and_8_out, not_4_out, in_2, in_3, in_4);
  and and_9 (and_9_out, in_1, not_3_out, not_2_out, not_1_out);
  and and_10 (and_10_out, in_1, not_3_out, not_2_out, in_4);
  and and_11 (and_11_out, in_1, not_3_out, in_3, in_4);
  and and_12 (and_12_out, in_1, not_3_out, in_3, not_1_out);
  and and_13 (and_13_out, in_1, not_1_out, not_2_out, not_1_out);
  and and_14 (and_14_out, in_1, in_2, not_2_out, in_4);
  and and_15 (and_15_out, not_1_out, in_1, in_2, in_3);
  and and_16 (and_16_out, in_1, in_2, in_3, in_4);
  or or_1 (or_1_out, and_16_out, and_15_out, and_13_out, and_11_out, and_12_out, and_10_out, and_9_out, and_7_out, and_6_out, and_5_out, and_1_out);
  or or_2 (or_2_out, and_16_out, and_15_out, and_14_out, and_11_out, and_12_out, and_10_out, and_9_out, and_7_out, and_6_out, and_5_out, and_3_out, and_4_out);
  or or_3 (or_3_out, and_16_out, and_15_out, and_14_out, and_13_out, and_11_out, and_12_out, and_9_out, and_7_out, and_4_out, and_1_out);
  or or_4 (or_4_out, and_15_out, and_14_out, and_13_out, and_11_out, and_10_out, and_9_out, and_7_out, and_6_out, and_3_out, and_4_out, and_1_out);
  _7_Segment_Display u_7_segment_display_1 (
    .g(or_2_out), .f(or_1_out), .a(or_5_out), .b(or_6_out), .e(or_3_out), .d(or_4_out), .c(or_7_out));  // open: dp
  or or_5 (or_5_out, and_16_out, and_15_out, and_13_out, and_12_out, and_10_out, and_9_out, and_8_out, and_7_out, and_6_out, and_3_out, and_4_out, and_1_out);
  or or_6 (or_6_out, and_14_out, and_12_out, and_10_out, and_9_out, and_8_out, and_5_out, and_3_out, and_4_out, and_2_out, and_1_out);
  or or_7 (or_7_out, and_14_out, and_11_out, and_12_out, and_10_out, and_9_out, and_8_out, and_7_out, and_6_out, and_5_out, and_3_out, and_2_out, and_1_out);
endmodule

module multiplexor (
  input  in_1,
  input  in_2,
  input  in_3,
  input  in_4,
  input  in_5,
  input  in_6,
  input  in_7,
  input  in_8,
  input  in_9,
  input  in_10,
  input  in_11,
  output out_12
);

  wire and_1_out, and_2_out, and_3_out, and_4_out, and_5_out, and_6_out, and_7_out, and_8_out, not_1_out,
       not_2_out, not_3_out, not_4_out, not_5_out, not_6_out, not_7_out, not_8_out, not_9_out, not_10_out,
       not_11_out, not_12_out;

  not not_1 (not_1_out, in_11);
  not not_2 (not_2_out, in_10);
  not not_3 (not_3_out, in_9);
  not not_4 (not_4_out, in_10);
  not not_5 (not_5_out, in_9);
  not not_6 (not_6_out, in_11);
  not not_7 (not_7_out, in_9);
  not not_8 (not_8_out, in_9);
  not not_9 (not_9_out, in_11);
  not not_10 (not_10_out, in_10);
  not not_11 (not_11_out, in_10);
  not not_12 (not_12_out, in_11);
  and and_1 (and_1_out, in_1, not_1_out, not_2_out, not_3_out);
  and and_2 (and_2_out, in_2, in_11, not_4_out, not_5_out);
  and and_3 (and_3_out, in_3, not_6_out, in_10, not_7_out);
  and and_4 (and_4_out, in_4, in_11, in_10, not_8_out);
  and and_5 (and_5_out, in_5, not_9_out, not_10_out, in_9);
  and and_6 (and_6_out, in_6, in_11, not_11_out, in_9);
  and and_7 (and_7_out, in_7, not_12_out, in_10, in_9);
  and and_8 (and_8_out, in_8, in_11, in_10, in_9);
  or or_1 (out_12, and_1_out, and_2_out, and_3_out, and_4_out, and_5_out, and_6_out, and_7_out, and_8_out);
endmodule

module demultiplexor (
  input  in_1,
  input  in_2,
  input  in_3,
  input  in_4,
  output out_5,
  output out_6,
  output out_7,
  output out_8,
  output out_9,
  output out_10,
  output out_11,
  output out_12
);

  wire not_1_out, not_2_out, not_3_out, not_4_out, not_5_out, not_6_out, not_7_out, not_8_out, not_9_out,
       not_10_out, not_11_out, not_12_out;

  not not_1 (not_1_out, in_4);
  not not_2 (not_2_out, in_3);
  not not_3 (not_3_out, in_2);
  not not_4 (not_4_out, in_3);
  not not_5 (not_5_out, in_2);
  not not_6 (not_6_out, in_4);
  not not_7 (not_7_out, in_2);
  not not_8 (not_8_out, in_2);
  not not_9 (not_9_out, in_4);
  not not_10 (not_10_out, in_3);
  not not_11 (not_11_out, in_3);
  not not_12 (not_12_out, in_4);
  and and_1 (out_5, in_1, not_1_out, not_2_out, not_3_out);
  and and_2 (out_6, in_1, in_4, not_4_out, not_5_out);
  and and_3 (out_7, in_1, not_6_out, in_3, not_7_out);
  and and_4 (out_8, in_1, in_4, in_3, not_8_out);
  and and_5 (out_9, in_1, not_9_out, not_10_out, in_2);
  and and_6 (out_10, in_1, in_4, not_11_out, in_2);
  and and_7 (out_11, in_1, not_12_out, in_3, in_2);
  and and_8 (out_12, in_1, in_4, in_3, in_2);
endmodule

module alu (
  input  [7:0] in_1,
  input  [7:0] in_2,
  input  in_3,
  input  in_4,
  input  in_5,
  output [7:0] out_6
);

  wire not_1_out, not_2_out, not_3_out, not_4_out, not_5_out, not_6_out, not_7_out, not_8_out, not_9_out,
       not_10_out, not_11_out, not_12_out;
  wire [7:0] and_9_out, and_10_out, and_11_out, and_12_out, and_13_out, and_14_out, and_15_out, and_16_out,
       and_17_out, n8adder_1_p6, n8adder_2_p7, or_1_out, shifter_1_out, shifter_2_out, shifter_3_out,
       xor_1_out;
  wire [7:7] and_1_out, and_2_out, and_3_out, and_4_out, and_5_out, and_6_out, and_7_out, and_8_out;

  not not_1 (not_1_out, in_5);
  not not_2 (not_2_out, in_4);
  not not_3 (not_3_out, in_3);
  not not_4 (not_4_out, in_4);
  not not_5 (not_5_out, in_3);
  not not_6 (not_6_out, in_5);
  not not_7 (not_7_out, in_3);
  not not_8 (not_8_out, in_3);
  not not_9 (not_9_out, in_5);
  not not_10 (not_10_out, in_4);
  not not_11 (not_11_out, in_4);
  not not_12 (not_12_out, in_5);
  and and_1 (and_1_out[7], not_1_out, not_2_out, not_3_out);
  and and_2 (and_2_out[7], in_5, not_4_out, not_5_out);
  and and_3 (and_3_out[7], not_6_out, in_4, not_7_out);
  and and_4 (and_4_out[7], in_5, in_4, not_8_out);
  and and_5 (and_5_out[7], not_9_out, not_10_out, in_3);
  and and_6 (and_6_out[7], in_5, not_11_out, in_3);
  and and_7 (and_7_out[7], not_12_out, in_4, in_3);
  and and_8 (and_8_out[7], in_5, in_4, in_3);
  // Probe on in_1
  // Probe on in_2
  // _8adder 8adder_1: pin names not known; wires that end beside it: 1'b0, and_1_out[7], in_1, in_2, and_1_out[7], n8adder_1_p6
  // _8adder 8adder_2: pin names not known; wires that end beside it: 1'b1, and_2_out[7], in_2, in_1, in_2, and_2_out[7], n8adder_2_p7
  assign and_9_out = in_1 & in_2;  // AND_Gate and_9, 8 bits wide
  assign or_1_out = in_1 | in_2;  // OR_Gate or_1, 8 bits wide
  assign xor_1_out = in_1 ^ in_2;  // XOR_Gate xor_1, 8 bits wide
  Shifter shifter_1 (.in(in_1), .\dist (in_2[2:0]), .out(shifter_1_out));
  Shifter #(.shift("lr")) shifter_2 (.in(in_1), .\dist (in_2[2:0]), .out(shifter_2_out));
  Shifter shifter_3 (.in(in_1), .\dist (in_2[2:0]), .out(shifter_3_out));
  assign and_10_out = {8{and_1_out[7]}} & n8adder_1_p6;  // AND_Gate and_10, 8 bits wide
  assign and_11_out = {8{and_2_out[7]}} & n8adder_2_p7;  // AND_Gate and_11, 8 bits wide
  assign and_12_out = {8{and_3_out[7]}} & and_9_out;  // AND_Gate and_12, 8 bits wide
  assign and_13_out = {8{and_4_out[7]}} & or_1_out;  // AND_Gate and_13, 8 bits wide
  assign and_14_out = {8{and_5_out[7]}} & xor_1_out;  // AND_Gate and_14, 8 bits wide
  assign and_15_out = {8{and_6_out[7]}} & shifter_1_out;  // AND_Gate and_15, 8 bits wide
  assign and_16_out = {8{and_7_out[7]}} & shifter_2_out;  // AND_Gate and_16, 8 bits wide
  assign and_17_out = {8{and_8_out[7]}} & shifter_3_out;  // AND_Gate and_17, 8 bits wide
  assign out_6 = and_10_out | and_11_out | and_12_out | and_13_out | and_14_out | and_15_out | and_16_out | and_17_out;  // OR_Gate or_2, 8 bits wide
endmodule

module halfadder (
  input  in_1,
  input  in_2,
  output out_3,
  output out_4
);

  and and_1 (out_3, in_1, in_2);
  xor xor_1 (out_4, in_1, in_2);
endmodule

module adder (
  input  in_1,
  input  in_2,
  input  in_3,
  output out_4,
  output out_5
);

  wire halfadder_1_out_3, halfadder_1_out_4, halfadder_2_out_3;

  halfadder halfadder_1 (.in_1(in_1), .in_2(in_2), .out_3(halfadder_1_out_3), .out_4(halfadder_1_out_4));
  halfadder halfadder_2 (.in_1(halfadder_1_out_4), .in_2(in_3), .out_3(halfadder_2_out_3), .out_4(out_4));
  or or_1 (out_5, halfadder_1_out_3, halfadder_2_out_3);
endmodule

module _8adder (
  input  [7:0] A,
  input  in_2,
  input  [7:0] B,
  output out_4,
  output [7:0] out_5
);

  wire adder_1_out_5, adder_2_out_5, adder_3_out_5, adder_4_out_5, adder_5_out_5, adder_6_out_5,
       adder_7_out_5;

  // Probe on A
  // Probe on B
  adder adder_1 (.in_1(A[0]), .in_2(B[0]), .in_3(in_2), .out_4(out_5[0]), .out_5(adder_1_out_5));
  adder adder_2 (.in_1(A[1]), .in_2(B[1]), .in_3(adder_1_out_5), .out_4(out_5[1]), .out_5(adder_2_out_5));
  adder adder_3 (.in_1(A[2]), .in_2(B[2]), .in_3(adder_2_out_5), .out_4(out_5[2]), .out_5(adder_3_out_5));
  // Probe on out_5
  adder adder_4 (.in_1(A[3]), .in_2(B[3]), .in_3(adder_3_out_5), .out_4(out_5[3]), .out_5(adder_4_out_5));
  adder adder_5 (.in_1(A[4]), .in_2(B[4]), .in_3(adder_4_out_5), .out_4(out_5[4]), .out_5(adder_5_out_5));
  adder adder_6 (.in_1(A[5]), .in_2(B[5]), .in_3(adder_5_out_5), .out_4(out_5[5]), .out_5(adder_6_out_5));
  adder adder_7 (.in_1(A[6]), .in_2(B[6]), .in_3(adder_6_out_5), .out_4(out_5[6]), .out_5(adder_7_out_5));
  adder adder_8 (.in_1(A[7]), .in_2(B[7]), .in_3(adder_7_out_5), .out_4(out_5[7]), .out_5(out_4));
endmodule

module \штм  (
  input  in_1,
  input  [7:0] in_2,
  output [7:0] out_3
);

  xor xor_1 (out_3[0], in_1, in_2[0]);
  xor xor_2 (out_3[1], in_1, in_2[1]);
  xor xor_3 (out_3[2], in_1, in_2[2]);
  xor xor_4 (out_3[3], in_1, in_2[3]);
  xor xor_5 (out_3[4], in_1, in_2[4]);
  xor xor_6 (out_3[5], in_1, in_2[5]);
  xor xor_7 (out_3[6], in_1, in_2[6]);
  xor xor_8 (out_3[7], in_1, in_2[7]);
endmodule

module RS_FLIP_FLOP (
  input  S,
  input  R,
  output minus_Q,
  output Q
);

  nor nor_1 (minus_Q, S, Q);
  nor nor_2 (Q, minus_Q, R);
endmodule

module sinc_rs_ff (
  input  S,
  input  C,
  input  R,
  output minus_Q,
  output Q
);

  wire and_1_out, and_2_out;

  and and_1 (and_1_out, S, C);
  and and_2 (and_2_out, C, R);
  nor nor_1 (minus_Q, and_1_out, Q);
  nor nor_2 (Q, minus_Q, and_2_out);
endmodule

module dflipflop_level (
  input  D,
  input  C,
  output minus_Q,
  output Q
);

  wire and_1_out, and_2_out, not_1_out;

  not not_1 (not_1_out, D);
  and and_1 (and_1_out, D, C);
  and and_2 (and_2_out, C, not_1_out);
  nor nor_1 (minus_Q, and_1_out, Q);
  nor nor_2 (Q, minus_Q, and_2_out);
endmodule

module dflipflop_front (
  input  D,
  input  C,
  output minus_Q,
  output Q
);

  wire and_1_out, and_2_out, and_3_out, and_4_out, nor_1_out, nor_2_out, not_1_out, not_2_out, not_3_out;

  not not_1 (not_1_out, C);
  not not_2 (not_2_out, D);
  and and_1 (and_1_out, D, not_1_out);
  and and_2 (and_2_out, not_1_out, not_2_out);
  nor nor_1 (nor_1_out, and_1_out, nor_2_out);
  nor nor_2 (nor_2_out, nor_1_out, and_2_out);
  not not_3 (not_3_out, nor_2_out);
  and and_3 (and_3_out, nor_2_out, C);
  and and_4 (and_4_out, C, not_3_out);
  nor nor_3 (minus_Q, and_3_out, Q);
  nor nor_4 (Q, minus_Q, and_4_out);
endmodule

module sinc_8_bit_reg (
  input  [7:0] in_1,
  input  in_2,
  output [7:0] out_3
);

  dflipflop_level dflipflop_level_1 (.D(in_1[7]), .C(in_2), .Q(out_3[7]));  // open: minus_Q
  dflipflop_level dflipflop_level_2 (.D(in_1[6]), .C(in_2), .Q(out_3[6]));  // open: minus_Q
  dflipflop_level dflipflop_level_3 (.D(in_1[5]), .C(in_2), .Q(out_3[5]));  // open: minus_Q
  dflipflop_level dflipflop_level_4 (.D(in_1[4]), .C(in_2), .Q(out_3[4]));  // open: minus_Q
  dflipflop_level dflipflop_level_5 (.D(in_1[3]), .C(in_2), .Q(out_3[3]));  // open: minus_Q
  dflipflop_level dflipflop_level_6 (.D(in_1[2]), .C(in_2), .Q(out_3[2]));  // open: minus_Q
  dflipflop_level dflipflop_level_7 (.D(in_1[1]), .C(in_2), .Q(out_3[1]));  // open: minus_Q
  dflipflop_level dflipflop_level_8 (.D(in_1[0]), .C(in_2), .Q(out_3[0]));  // open: minus_Q
endmodule

module _4_sinc_thing (
  input  in_1,
  output [3:0] out_2
);

  wire [3:0] dflipflop_front_4_q;

  dflipflop_front dflipflop_front_1 (.D(out_2[3]), .C(in_1), .Q(dflipflop_front_4_q[3]));  // open: minus_Q
  dflipflop_front dflipflop_front_2 (.D(out_2[2]), .C(in_1), .Q(dflipflop_front_4_q[2]));  // open: minus_Q
  dflipflop_front dflipflop_front_3 (.D(out_2[1]), .C(in_1), .Q(dflipflop_front_4_q[1]));  // open: minus_Q
  dflipflop_front dflipflop_front_4 (.D(out_2[0]), .C(in_1), .Q(dflipflop_front_4_q[0]));  // open: minus_Q
  _4ADDER u_4adder_1 (.A(dflipflop_front_4_q), .in_2(1'b1), .B(4'b0000), .out_4(out_2));  // open: out_5
endmodule

module _4ADDER (
  input  [3:0] A,
  input  in_2,
  input  [3:0] B,
  output [3:0] out_4,
  output out_5
);

  wire adder_1_out_5, adder_2_out_5, adder_3_out_5;

  adder adder_1 (.in_1(A[0]), .in_2(B[0]), .in_3(in_2), .out_4(out_4[0]), .out_5(adder_1_out_5));
  adder adder_2 (.in_1(A[1]), .in_2(B[1]), .in_3(adder_1_out_5), .out_4(out_4[1]), .out_5(adder_2_out_5));
  adder adder_3 (.in_1(A[2]), .in_2(B[2]), .in_3(adder_2_out_5), .out_4(A[3]), .out_5(adder_3_out_5));
  adder adder_4 (.in_1(A[3]), .in_2(B[3]), .in_3(adder_3_out_5), .out_4(out_4[3]), .out_5(out_5));

  assign out_4[2] = A[3];
endmodule

module _8adder_cool (
  input  in_1,
  input  [7:0] in_2,
  input  Sel,
  input  [7:0] in_4,
  output [7:0] out_5,
  output out_6,
  output [7:0] out_7
);

  wire [7:0] and_1_out, and_2_out, not_2_out, or_1_out;
  wire [7:7] not_1_out;

  // Probe on in_4
  // Probe on in_2
  _8adder u_8adder_1 (.A(in_4), .in_2(1'b0), .out_4(out_6), .B(or_1_out), .out_5(out_7));
  // Probe on out_7
  assign and_1_out = in_2 & {8{not_1_out[7]}};  // AND_Gate and_1, 8 bits wide
  assign or_1_out = and_1_out | and_2_out;  // OR_Gate or_1, 8 bits wide
  not not_1 (not_1_out[7], Sel);
  assign not_2_out = ~{8{not_1_out[7]}};  // NOT_Gate not_2, 8 bits wide
  assign and_2_out = not_2_out & out_5;  // AND_Gate and_2, 8 bits wide
  // Probe on out_5
  sinc_8_bit_reg sinc_8_bit_reg_1 (.in_2(in_1), .in_1(out_7), .out_3(out_5));
endmodule

module _8adder_with_accum (
  input  [7:0] in_1,
  input  in_2,
  output [7:0] out_3,
  output [7:0] out_4
);

  // Probe on in_1
  _8adder u_8adder_1 (.A(in_1), .in_2(1'b0), .B(out_3), .out_5(out_4));  // open: out_4
  // Probe on out_4
  sinc_8_bit_reg sinc_8_bit_reg_1 (.in_2(in_2), .in_1(out_4), .out_3(out_3));
  // Probe on out_3
endmodule

module RAM (
  input  in_1,
  input  [7:0] A,
  input  in_3,
  input  R,
  input  [2:0] Sel,
  output [7:0] out_6
);

  wire and_1_out, decoder_1_out0, decoder_1_out1, decoder_1_out2, decoder_1_out3, decoder_1_out4,
       decoder_1_out5, decoder_1_out6, decoder_1_out7;
  wire [7:0] register_1_q, register_2_q, register_3_q, register_4_q, register_5_q, register_6_q,
       register_7_q, register_8_q;

  and and_1 (and_1_out, in_1, in_3);
  Decoder #(.select(3)) decoder_1 (
    .out0(decoder_1_out0), .out1(decoder_1_out1), .out2(decoder_1_out2), .out3(decoder_1_out3),
    .out4(decoder_1_out4), .out5(decoder_1_out5), .out6(decoder_1_out6), .out7(decoder_1_out7), .sel(Sel));  // open: en
  Register #(.trigger("falling")) register_1 (.D(A), .en(decoder_1_out1), .Q(register_1_q), .clk(and_1_out), .clr(R));
  Register #(.trigger("falling")) register_2 (.D(A), .en(decoder_1_out0), .Q(register_2_q), .clk(and_1_out), .clr(R));
  Register #(.trigger("falling")) register_3 (.D(A), .en(decoder_1_out2), .Q(register_3_q), .clk(and_1_out), .clr(R));
  Register #(.trigger("falling")) register_4 (.D(A), .en(decoder_1_out3), .Q(register_4_q), .clk(and_1_out), .clr(R));
  Register #(.trigger("falling")) register_5 (.D(A), .en(decoder_1_out5), .Q(register_5_q), .clk(and_1_out), .clr(R));
  Register #(.trigger("falling")) register_6 (.D(A), .en(decoder_1_out4), .Q(register_6_q), .clk(and_1_out), .clr(R));
  Register #(.trigger("falling")) register_7 (.D(A), .en(decoder_1_out6), .Q(register_7_q), .clk(and_1_out), .clr(R));
  Register #(.trigger("falling")) register_8 (.D(A), .en(decoder_1_out7), .Q(register_8_q), .clk(and_1_out), .clr(R));
  Multiplexer #(.select(3), .width(8)) multiplexer_1 (
    .in0(register_2_q), .in1(register_1_q), .in2(register_3_q), .in3(register_4_q), .in4(register_6_q),
    .in5(register_5_q), .in6(register_7_q), .in7(register_8_q), .out(out_6), .sel(Sel));  // open: en

  // Notes on the sheet:
  //   WE
  //   CLK
  //   out
endmodule
